# Fritzing sketch midiboard (saved by Fritzing 0.9.2b)
breadboards: 1

parts:
  Componente1 = Arduino Uno (Rev3)
  S1 = Pushbutton [package="[THT]"]
  S2 = Pushbutton [package="[THT]"]
  LED1 = LED - 5mm [color="Green (565nm)" package="5 mm [THT]"]
  LED2 = LED - 5mm [color="Green (565nm)" package="5 mm [THT]"]
  R1 = Resistor [tolerance=±5% resistance=220 package=THT]
  R2 = Resistor [tolerance=±5% resistance=220 package=THT]
  Digit_6 = 7 Segment Display  # not connected
  Digit_5 = 7 Segment Display  # not connected
  Digit_7 = 7 Segment Display  # not connected
  Digit_8 = 7 Segment Display  # not connected
  S3 = Pushbutton [package="[THT]"]
  S4 = Pushbutton [package="[THT]"]
  DIN1 = DIN-5 jack (MIDI) [package=THT]
  R3 = Resistor [tolerance=±5% resistance=220 package=THT]

nets:
  N1: Componente1.A0, R1.Pin_1
  N2: Componente1.A1, R2.Pin_1
  N3: Componente1.A2, S1.Pin_3, S1.Pin_4
  N4: Componente1.A3, S2.Pin_3, S2.Pin_4
  N5: Componente1.A4/SDA, S3.Pin_3, S3.Pin_4
  N6: Componente1.A5/SCL, S4.Pin_3, S4.Pin_4
  N7: Componente1.D1/TX, DIN1.5
  N8: Componente1.5V, R3.Pin_0
  N9: Componente1.GND, S1.Pin_1, S1.Pin_2, S2.Pin_1, S2.Pin_2, LED1.cathode, LED2.cathode, S3.Pin_1, S3.Pin_2, S4.Pin_1, S4.Pin_2, DIN1.2, DIN1.1
  N10: Componente1.VIN, DIN1.3
  N11: LED1.anode, R1.Pin_0
  N12: LED2.anode, R2.Pin_0
  N13: DIN1.4, R3.Pin_1
